# Fritzing sketch sketch (saved by Fritzing 0.9.3b)
breadboards: 2

parts:
  S1 = H-Bridge with L298N
  BT1 = Bluetooth HC-06u [package=THT]
  부품1 = Arduino Uno (Rev3)
  M1 = DC Motor
  M2 = DC Motor
  Power_plug1 = Power plug [part_number="12V 2A"]
  Part1 = KY-015 Temperature & Humidity Sensor Module [package="Breakout board"]
  부품2 = ws2812b [package="smd 2812b"]
  부품3 = ws2812b [package="smd 2812b"]
  부품4 = ws2812b [package="smd 2812b"]
  부품5 = ws2812b [package="smd 2812b"]

nets:
  12V: S1.12V, Power_plug1.VCC
  GND: S1.GND, BT1.GND, 부품1.GND, Power_plug1.GND, Part1.-, 부품2.VSS, 부품3.VSS, 부품4.VSS, 부품5.VSS
  5V: S1.5V, 부품1.VIN
  N1: S1.IN1, 부품1.D6_PWM
  N2: S1.IN2, 부품1.D7
  N3: S1.IN3, 부품1.D11_PWM/MOSI
  N4: S1.IN4, 부품1.D12/MISO
  N5: S1.M1-01, M1.pin_1
  N6: S1.M1-02, M1.pin_2
  N7: S1.M2-01, M2.pin_2
  N8: S1.M2-02, M2.pin_1
  VDD: BT1.VCC, 부품1.5V, Part1.Vin, 부품2.VDD, 부품3.VDD, 부품4.VDD, 부품5.VDD
  N9: BT1.TXD, 부품1.D2
  N10: BT1.RXD, 부품1.D3_PWM
  N11: 부품1.D4, Part1.S
  N12: 부품1.D5_PWM, 부품4.DIN
  N13: 부품2.DOUT, 부품5.DIN
  N14: 부품2.DIN, 부품3.DOUT
  N15: 부품3.DIN, 부품4.DOUT

custom parts:
  H-Bridge with L298N: h-bridge
  Bluetooth HC-06u: Bluetooth HC-06 - face up, pins down 16.5mm x 37.5mm PCB
  KY-015 Temperature & Humidity Sensor Module: KY-015 temperature and humidity sensor module, provides a low-latency serial interface to measure humidity and temperature.
